# Fritzing sketch shema-lodka (saved by Fritzing 0.9.4)

parts:
  Часть1 = Arduino Micro (Rev3)
  Grove1 = Grove OLED 128x96
  VCC1 = Battery block 9V  # not connected
  M4 = ESC
  920KV_Motor4 = DJI 920 KV Motor
  Компонент1 = Black Joystick KY-023

nets:
  GND: Часть1.GND, Grove1.GND, M4.GND, Компонент1.GND
  N1: Часть1.D8_PWM/A8, Компонент1.SW
  N2: Часть1.D9_PWM/A9, M4.DATA
  5V: Часть1.5V, M4.5V, Компонент1.+5V
  N3: Часть1.A1, Компонент1.VRx
  3V3: Часть1.3V3, Grove1.VCC
  N4: M4.U, 920KV_Motor4.u
  N5: M4.V, 920KV_Motor4.v
  N6: M4.W, 920KV_Motor4.w

custom parts:
  DJI 920 KV Motor: DJI Brushless Outrunner 2212/920K Motor F330-550
  Black Joystick KY-023: Description: The joystick is a combination of 2 analoog potentiometer and a digital switch. Arduino GND --> Module pin - Arduino +5V --> Module pin +5V Arduino Analoog 0 --> Module VRx Arduino Analoog 1 --> Module VRy Arduino Digital --> Module SW Dimensions: 1" x 1.25"
